# Fritzing sketch Connecting (saved by Fritzing 0.9.3b)
breadboards: 1

parts:
  U1 = NodeMCU V1.0
  RGB_SMD_LED1 = SMD RGB LED (WS2812) [package=5050]
  RGB_SMD_LED2 = SMD RGB LED (WS2812) [package=5050]
  RGB_SMD_LED3 = SMD RGB LED (WS2812) [package=5050]
  RGB_SMD_LED4 = SMD RGB LED (WS2812) [package=5050]
  RGB_SMD_LED5 = SMD RGB LED (WS2812) [package=5050]
  RGB_SMD_LED6 = SMD RGB LED (WS2812) [package=5050]
  RGB_SMD_LED7 = SMD RGB LED (WS2812) [package=5050]
  RGB_SMD_LED8 = SMD RGB LED (WS2812) [package=5050]
  RGB_SMD_LED9 = SMD RGB LED (WS2812) [package=5050]
  RGB_SMD_LED10 = SMD RGB LED (WS2812) [package=5050]
  RGB_SMD_LED11 = SMD RGB LED (WS2812) [package=5050]
  RGB_SMD_LED12 = SMD RGB LED (WS2812) [package=5050]
  RGB_SMD_LED13 = SMD RGB LED (WS2812) [package=5050]
  RGB_SMD_LED14 = SMD RGB LED (WS2812) [package=5050]
  RGB_SMD_LED15 = SMD RGB LED (WS2812) [package=5050]
  RGB_SMD_LED16 = SMD RGB LED (WS2812) [package=5050]

nets:
  VSS: U1.GND, RGB_SMD_LED1.VSS, RGB_SMD_LED2.VSS, RGB_SMD_LED3.VSS, RGB_SMD_LED4.VSS, RGB_SMD_LED5.VSS, RGB_SMD_LED6.VSS, RGB_SMD_LED7.VSS, RGB_SMD_LED8.VSS
  N1: U1.D5, RGB_SMD_LED1.DIn
  VIN: U1.Vin, RGB_SMD_LED1.VDD
  N2: RGB_SMD_LED1.DOut, RGB_SMD_LED2.DIn
  N3: RGB_SMD_LED2.DOut, RGB_SMD_LED3.DIn
  VDD: RGB_SMD_LED2.VDD, RGB_SMD_LED3.VDD, RGB_SMD_LED4.VDD, RGB_SMD_LED5.VDD, RGB_SMD_LED6.VDD, RGB_SMD_LED7.VDD, RGB_SMD_LED8.VDD
  N4: RGB_SMD_LED3.DOut, RGB_SMD_LED4.DIn
  N5: RGB_SMD_LED4.DOut, RGB_SMD_LED5.DIn
  N6: RGB_SMD_LED5.DOut, RGB_SMD_LED6.DIn
  N7: RGB_SMD_LED6.DOut, RGB_SMD_LED7.DIn
  N8: RGB_SMD_LED7.DOut, RGB_SMD_LED8.DIn
  N9: RGB_SMD_LED9.DOut, RGB_SMD_LED10.DIn
  N10: RGB_SMD_LED10.DOut, RGB_SMD_LED11.DIn
  N11: RGB_SMD_LED11.DOut, RGB_SMD_LED12.DIn
  N12: RGB_SMD_LED12.DOut, RGB_SMD_LED13.DIn
  N13: RGB_SMD_LED13.DOut, RGB_SMD_LED14.DIn
  N14: RGB_SMD_LED14.DOut, RGB_SMD_LED15.DIn
  N15: RGB_SMD_LED15.DOut, RGB_SMD_LED16.DIn

notes:
  Instead of VIN while using USB, it's recommended to use a proper PSU. It can work for a very small amount of LED's.
  #0
  #7
  Daisy Chain
  If you connect the white wire, the LED's become #0 - #7 as well. It means, they shine in the same color, in same order, than the LED's connected with the black wire.
  No need for this until you need more brightness :D

custom parts:
  NodeMCU V1.0: ESP8266 based NodeMCU
